# Fritzing sketch led-logical-gates (saved by Fritzing 0.9.3b)
breadboards: 1

parts:
  Part1 = Arduino Uno (Rev3)
  S1 = Momentary Switch [package=ksa_sealed_tac_switch]
  S2 = Momentary Switch [package=ksa_sealed_tac_switch]
  LED1 = LED - 3mm [color="Red (633nm)" package="3 mm [THT]"]
  R1 = Resistor [tolerance=±5% resistance=220 package="0805 [SMD]"]

nets:
  N1: Part1.D8, S2.3
  N2: Part1.D9_PWM, S1.3
  N3: Part1.D13/SCK, LED1.anode
  N4: Part1.GND, S1.1, S2.1, R1.Pin_1
  N5: LED1.cathode, R1.Pin_0
