# Fritzing sketch toggle-led-with-button (saved by Fritzing 0.9.3b)
breadboards: 1

parts:
  Part1 = Arduino Uno (Rev3)
  S2 = Pushbutton [package="[SMD]"]
  LED1 = smd LED [color="Red (633nm)" package="0805 [SMD]"]
  R1 = Resistor [tolerance=±5% resistance=220 package=THT]

nets:
  N1: Part1.D8, S2.Pin_3, S2.Pin_4
  N2: Part1.D13/SCK, LED1.anode
  N3: Part1.GND, S2.Pin_1, S2.Pin_2, R1.Pin_1
  N4: LED1.cathode, R1.Pin_0
